// Logisim project Processor.circ as structural Verilog: 3 circuits, main circuit main
module main (
);

  ULA ula_1 ();  // open: F2, F1, F0, A, B, C
endmodule

module ULA (
  input  [7:0] A,
  input  F2,
  input  F1,
  input  F0,
  input  [7:0] B,
  output [7:0] C
);

  wire [7:0] adder_1_out, adder_2_out, adder_3_out, and_1_out, or_1_out, subtractor_1_out;

  Adder adder_1 (.a(A), .b(8'h1), .out(adder_1_out));  // open: cin, cout
  Adder adder_2 (.a(B), .b(8'h1), .out(adder_2_out));  // open: cin, cout
  Adder adder_3 (.a(A), .b(B), .out(adder_3_out));  // open: cin, cout
  Subtractor subtractor_1 (.a(A), .b(B), .out(subtractor_1_out));  // open: bin, bout
  assign and_1_out = A & B;  // AND_Gate and_1, 8 bits wide
  assign or_1_out = A | B;  // OR_Gate or_1, 8 bits wide
  Multiplexer #(.select(3), .width(8)) multiplexer_1 (
    .in0(A), .in1(B), .in2(adder_1_out), .in3(adder_2_out), .in4(adder_3_out), .in5(subtractor_1_out),
    .in6(and_1_out), .in7(or_1_out), .out(C), .sel({F2, F1, F0}));  // open: en
endmodule

// A
module Datapath (
  input  in_1,
  input  in_2,
  input  in_3,
  input  in_4,
  input  in_5,
  input  in_6,
  input  in_7,
  input  in_8,
  input  in_9,
  input  in_10,
  input  [7:0] External_Input
);

  wire clock_1_out;
  wire [7:0] A_q, B_q, MBR_q, multiplexer_1_out, PC_q, ula_1_c;

  Clock clock_1 (.out(clock_1_out));
  Register A (.D(ula_1_c), .en(in_5), .Q(A_q), .clk(clock_1_out));  // open: clr
  Register B (.D(ula_1_c), .en(in_4), .Q(B_q), .clk(clock_1_out));  // open: clr
  Register MBR (.en(in_3), .Q(MBR_q), .clk(clock_1_out));  // open: D, clr
  Register PC (.D(ula_1_c), .en(in_2), .Q(PC_q), .clk(clock_1_out));  // open: clr
  Register OUT (.D(ula_1_c), .en(in_1), .clk(clock_1_out));  // open: Q, clr
  Multiplexer #(.select(2), .width(8)) multiplexer_1 (
    .in0(B_q), .in1(MBR_q), .in2(PC_q), .in3(External_Input), .out(multiplexer_1_out), .sel({in_9, in_10}),
    .en(1'b1));
  ULA ula_1 (.F2(in_6), .F1(in_7), .F0(in_8), .A(A_q), .B(multiplexer_1_out), .C(ula_1_c));
endmodule
